// Logisim project SudeÇakmak_152120201044_Lab3_2 .circ as structural Verilog: 1 circuit, main circuit main
module main (
  input  C,
  input  D,
  input  B,
  input  A,
  output out_5
);

  wire not_1_out, xor_1_out;

  xor xor_1 (xor_1_out, C, D);
  not not_1 (not_1_out, xor_1_out);
  Multiplexer #(.select(2), .enable("false")) multiplexer_1 (
    .in0(xor_1_out), .in1(not_1_out), .in2(not_1_out), .in3(xor_1_out), .out(out_5), .sel({A, B}));
endmodule
