// Logisim project Sude_Çakmak_Lab4_FullAdder.circ as structural Verilog: 1 circuit, main circuit main
module main (
  input  INPUT_A,
  input  INPUT_B,
  input  CARRY_in,
  output SUM,
  output CARRY_out
);

  wire nand_1_out, nand_2_out, xor_1_out;

  xor xor_1 (xor_1_out, INPUT_A, INPUT_B);
  nand nand_1 (nand_1_out, INPUT_A, INPUT_B);
  xor xor_2 (SUM, xor_1_out, CARRY_in);
  nand nand_2 (nand_2_out, CARRY_in, xor_1_out);
  nand nand_3 (CARRY_out, nand_2_out, nand_1_out);
endmodule
